# Fritzing sketch RGB_LED_Shield (saved by Fritzing 0.9.3b)
circuit board: 4cm x 5.4cm
breadboards: 1

parts:
  J1 = Camdenboss CTB0158-4 [part_number=CTB0158-4 package=THT]
  Q2 = Basic FET N-Channel [package="TO220 [THT]"]
  Q3 = Basic FET N-Channel [package="TO220 [THT]"]
  Q1 = Basic FET N-Channel [package="TO220 [THT]"]
  J2 = Power Jack [package=power_jack_slot]
  Part1 = Arduino Uno (Rev3)

nets:
  N1: J1.pin1, J2.PWR, Part1.VIN
  N2: J1.pin2, Q1.drain
  N3: J1.pin3, Q3.drain
  N4: J1.pin4, Q2.drain
  N5: Q2.gate, Part1.D3_PWM
  GND: Q2.source, Q3.source, Q1.source, J2.GND, Part1.GND
  N6: Q3.gate, Part1.D5_PWM
  N7: Q1.gate, Part1.D6_PWM
